// Digital circuit UTS 2.dig as structural Verilog
module UTS_2 (
  input  A,
  input  B,
  input  C,
  input  C_2
);

  wire and_1_out, and_2_out, and_3_out, and_4_out, and_5_out, and_6_out, not_1_out, not_2_out, not_3_out,
       not_4_out, not_5_out, not_6_out, not_7_out, not_8_out, not_9_out, or_1_out;

  not not_1 (not_1_out, A);
  not not_2 (not_2_out, B);
  not not_3 (not_3_out, C_2);
  not not_4 (not_4_out, A);
  not not_5 (not_5_out, A);
  not not_6 (not_6_out, A);
  // Not not_7 has open pins: in=open, out=not_7_out
  not not_8 (not_8_out, A);
  not not_9 (not_9_out, C_2);
  and and_1 (and_1_out, not_1_out, not_2_out, not_3_out);
  and and_2 (and_2_out, not_4_out, C);  // open: In_2
  and and_3 (and_3_out, not_5_out, not_6_out, not_7_out);
  and and_4 (and_4_out, not_8_out, B, C);
  and and_5 (and_5_out, A, B, C_2);
  and and_6 (and_6_out, A, B, not_9_out);
  or or_1 (or_1_out, and_1_out, and_2_out, and_3_out, and_4_out, and_5_out, and_6_out);
  LED X (.in(or_1_out));
endmodule
